# Fritzing sketch wireless-estop-base (saved by Fritzing 0.9.3b)

parts:
  WeMos_D1_Mini3 = WeMos D1 Mini
  Mod2 = KY-019 5V Relay Module [package="Breakout board"]

nets:
  N1: WeMos_D1_Mini3.5V, Mod2.+
  N2: WeMos_D1_Mini3.D2, Mod2.S
  N3: WeMos_D1_Mini3.G, Mod2.-

custom parts:
  KY-019 5V Relay Module: KY-019 5V Relay module, used to control AC circuits. (Special thanks to vanepp for fixing the PCB holes and other errors)
