# Fritzing sketch remote-estop (saved by Fritzing 0.9.3b)

parts:
  S1 = Round Pushbutton
  WeMos_D1_Mini1 = WeMos D1 Mini
  R1 = Resistor [tolerance=±5% resistance=10k package=THT]
  R2 = Resistor [tolerance=±5% resistance=10k package=THT]
  WeMos_D1_Mini_Battery_Shield1 = WeMos D1 Mini Battery Shield

nets:
  N1: S1.leg0, WeMos_D1_Mini1.3V3
  N2: S1.leg1, WeMos_D1_Mini1.D2, R1.Pin_1
  5V: WeMos_D1_Mini1.5V, WeMos_D1_Mini_Battery_Shield1.5V
  N3: WeMos_D1_Mini1.A0, R2.Pin_0
  N4: WeMos_D1_Mini1.G, R1.Pin_0, WeMos_D1_Mini_Battery_Shield1.G
